// Logisim project CPU.circ as structural Verilog: 2 circuits, main circuit main
module main (
  input  RST
);

  wire ADD, ADDI, alu_1_zero, and_1_out, and_2_out, bit_extender_6_out, button_1_out, button_2_out,
       button_3_out, button_4_out, CLK, COUT, decoder_1_out1, decoder_1_out2, decoder_1_out3, decoder_1_out4,
       decoder_1_out5, decoder_3_out1, decoder_3_out2, decoder_3_out3, decoder_3_out4, IMMEDIATE_SET, INP,
       IS_ALU, JC, JUMP, JZ, LOAD, MOV, MOVI, multiplexer_5_out, NOP, or_1_out, or_2_out, OUT_SET, PC_INC,
       RAM_SET, REG_SET, ROTLI, ROTRI, SEL0, SEL1, SHLI, SHRI, SUB, SUBI, ZERO;
  wire [2:0] bit_extender_3_out, bit_extender_4_out;
  wire [4:0] bit_extender_2_out, REG_ADDR, REGY;
  wire [5:0] and_3_out, bit_extender_1_out, OPCODE, subtractor_1_out;
  wire [15:0] A_q, adder_1_out, ALU_OUT, B, B_q, C_q, D_q, E_q, IMM16, IN_OUT, multiplexer_1_out, PC,
       RAM_OUT, REG_IN, register_4_q, register_5_q, register_6_q, register_7_q, REGX_OUT, REGY_OUT;
  wire [31:0] rom_1_data;

  Adder #(.width(16)) adder_1 (.a(PC), .b(16'h1), .out(adder_1_out));  // open: cin, cout
  // Probe on PC
  // Probe on REGX_OUT
  Multiplexer #(.width(16)) multiplexer_1 (.in0(IMM16), .in1(adder_1_out), .out(multiplexer_1_out), .sel(PC_INC));
  and and_1 (and_1_out, JZ, ZERO);
  and and_2 (and_2_out, JC, COUT);
  ROM #(.addrWidth(16), .dataWidth(32)) rom_1 (.addr(PC), .data(rom_1_data));
  RAM #(.addrWidth(16), .asyncread("true"), .dataWidth(16)) ram_1 (
    .addr(B), .we(RAM_SET), .oe(1'b1), .clk(CLK), .din(REGX_OUT), .dout(RAM_OUT));
  Clock clock_1 (.out(CLK));
  Register #(.trigger("falling"), .width(16)) register_1 (
    .D(multiplexer_1_out), .en(1'b1), .clk(CLK), .Q(PC), .clr(RST));
  or or_1 (or_1_out, JUMP, and_1_out, and_2_out);
  not not_1 (PC_INC, or_1_out);
  // Probe on rom_1_data
  or or_2 (or_2_out, ADDI, SUBI);
  Decoder #(.select(5)) decoder_1 (
    .out1(decoder_1_out1), .out2(decoder_1_out2), .out3(decoder_1_out3), .out4(decoder_1_out4),
    .out5(decoder_1_out5), .sel(REG_ADDR), .en(REG_SET));  // open: out0, out6, out7, out8, out9, out10, out11, out12, out13, out14, out15, out16, out17, out18, out19, out20, out21, out22, out23, out24, out25, out26, out27, out28, out29, out30, out31
  // Probe on OPCODE
  assign bit_extender_1_out = {{5{or_2_out}}, or_2_out};  // Bit_Extender bit_extender_1
  Register #(.width(32)) register_2 (
    .D(rom_1_data), .en(1'b1), .clk(CLK), .Q({OPCODE, REG_ADDR, REGY, IMM16}), .clr(RST));
  Subtractor #(.width(6)) subtractor_1 (.a(OPCODE), .b(and_3_out), .out(subtractor_1_out));  // open: bin, bout
  assign and_3_out = bit_extender_1_out & 6'b000100;  // AND_Gate and_3, 6 bits wide
  // Probe on REG_IN
  Register #(.width(16)) A (.D(REG_IN), .en(decoder_1_out1), .clk(CLK), .Q(A_q), .clr(RST));
  Register #(.width(16)) u_B (.D(REG_IN), .en(decoder_1_out2), .clk(CLK), .Q(B_q), .clr(RST));
  Register #(.width(16)) C (.D(REG_IN), .en(decoder_1_out3), .clk(CLK), .Q(C_q), .clr(RST));
  Register #(.width(16)) D (.D(REG_IN), .en(decoder_1_out4), .clk(CLK), .Q(D_q), .clr(RST));
  Register #(.width(16)) E (.D(REG_IN), .en(decoder_1_out5), .clk(CLK), .Q(E_q), .clr(RST));
  // Probe on subtractor_1_out[3:0]
  Decoder #(.select(5)) decoder_2 (
    .out0(NOP), .out4(SHRI), .out5(SHLI), .out6(ROTRI), .out7(ROTLI), .out8(ADD), .out9(SUB), .out12(ADDI),
    .out13(SUBI), .out16(LOAD), .out17(RAM_SET), .out18(INP), .out19(OUT_SET), .out20(JUMP), .out21(JZ),
    .out22(JC), .out23(MOV), .out24(MOVI), .sel(bit_extender_2_out), .en(1'b1));  // open: out1, out2, out3, out10, out11, out14, out15, out25, out26, out27, out28, out29, out30, out31
  Bit_Extender #(.in_width(6), .out_width(5)) bit_extender_2 (.in(OPCODE), .out(bit_extender_2_out));
  // Probe on bit_extender_2_out
  Multiplexer #(.select(5), .width(16)) multiplexer_2 (
    .in1(A_q), .in2(B_q), .in3(C_q), .in4(D_q), .in5(E_q), .out(REGX_OUT), .sel(REG_ADDR));  // open: in0, in6, in7, in8, in9, in10, in11, in12, in13, in14, in15, in16, in17, in18, in19, in20, in21, in22, in23, in24, in25, in26, in27, in28, in29, in30, in31
  ALU alu_1 (
    .A(REGX_OUT), .B(B), .CIN(1'b0), .SEL(subtractor_1_out[3:0]), .OUTP(ALU_OUT), .COUT(COUT),
    .ZERO(alu_1_zero));  // open: OVER, SIGN, HOUT, LT, GT, EQ
  // Probe on REGX_OUT
  Register #(.width(1)) register_3 (.D(alu_1_zero), .en(IS_ALU), .clk(CLK), .Q(ZERO), .clr(RST));
  Multiplexer #(.select(5), .width(16)) multiplexer_3 (
    .in1(A_q), .in2(B_q), .in3(C_q), .in4(D_q), .in5(E_q), .out(REGY_OUT), .sel(REGY));  // open: in0, in6, in7, in8, in9, in10, in11, in12, in13, in14, in15, in16, in17, in18, in19, in20, in21, in22, in23, in24, in25, in26, in27, in28, in29, in30, in31
  // Probe on REGY_OUT
  // Probe on IN_OUT
  Button button_1 (.out(button_1_out));
  Button button_2 (.out(button_2_out));
  Button button_3 (.out(button_3_out));
  // Probe on B
  or or_3 (SEL1, INP, MOV);
  or or_4 (SEL0, LOAD, MOV);
  Button button_4 (.out(button_4_out));
  or or_5 (IS_ALU, SHRI, SHLI, ROTRI, ROTLI, ADD, SUB, ADDI, SUBI);
  or or_6 (REG_SET, SHRI, SHLI, ROTRI, ROTLI, ADD, SUB, ADDI, SUBI, LOAD, INP, MOV, MOVI);
  or or_7 (IMMEDIATE_SET, SHRI, SHLI, ROTRI, ROTLI, MOVI, ADDI, SUBI);
  Multiplexer #(.width(16)) multiplexer_4 (.in0(REGY_OUT), .in1(IMM16), .out(B), .sel(IMMEDIATE_SET));
  Bit_Extender #(.in_width(16), .out_width(3)) bit_extender_3 (.in(B), .out(bit_extender_3_out));
  Decoder #(.select(3)) decoder_3 (
    .out1(decoder_3_out1), .out2(decoder_3_out2), .out3(decoder_3_out3), .out4(decoder_3_out4),
    .sel(bit_extender_4_out), .en(OUT_SET));  // open: out0, out5, out6, out7
  Bit_Extender #(.in_width(16), .out_width(3)) bit_extender_4 (.in(B), .out(bit_extender_4_out));
  // Probe on REGY_OUT
  // Probe on IMM16
  Multiplexer #(.select(3)) multiplexer_5 (
    .in0(1'b0), .in1(button_1_out), .in2(button_2_out), .in3(button_3_out), .in4(button_4_out), .in5(1'b0),
    .in6(1'b0), .in7(1'b0), .out(multiplexer_5_out), .sel(bit_extender_3_out));
  // Probe on REG_IN
  Multiplexer #(.select(3), .width(16)) multiplexer_6 (
    .in0(ALU_OUT), .in1(IMM16), .in2(IN_OUT), .in4(RAM_OUT), .in6(REGY_OUT), .out(REG_IN),
    .sel({SEL0, SEL1, MOVI}));  // open: in3, in5, in7
  // Probe on {SEL0, SEL1, MOVI}
  assign IN_OUT = {{15{1'b0}}, multiplexer_5_out};  // Bit_Extender bit_extender_5
  // Probe on REGX_OUT
  Register #(.width(16)) register_4 (.D(REGX_OUT), .en(decoder_3_out1), .clk(CLK), .Q(register_4_q), .clr(RST));
  Register #(.width(16)) register_5 (.D(REGX_OUT), .en(decoder_3_out2), .clk(CLK), .Q(register_5_q), .clr(RST));
  Register #(.width(16)) register_6 (.D(REGX_OUT), .en(decoder_3_out3), .clk(CLK), .Q(register_6_q), .clr(RST));
  Register #(.width(16)) register_7 (.D(REGX_OUT), .en(decoder_3_out4), .clk(CLK), .Q(register_7_q), .clr(RST));
  Bit_Extender #(.in_width(16), .out_width(1)) bit_extender_6 (.in(register_7_q), .out(bit_extender_6_out));
  DotMatrix #(.matrixcols(3), .matrixrows(16)) dotmatrix_1 (
    .col0(register_4_q), .col1(register_5_q), .col2(register_6_q));
  LED led_1 (.in(bit_extender_6_out));

  // Other names for the same wires on the sheet: JMP[15:0] = IMM16; REGX[4:0] = REG_ADDR; SEL2 = MOVI; OUTP = OUT_SET;
  //   STORE = RAM_SET

  // Notes on the sheet:
  //   contents of rom_1 (hex, n*v repeats v):
  //   60200002 60400001 4c410000 60800001 48640000 5ca30000 34a00001 5400000e 60800003 48640000 5ca30000
  //   34a00001 54000010 50000002 14400001 50000002 10400001 50000002
endmodule

module comments (
);

  wire CLK, decoder_1_out8, decoder_1_out9, decoder_1_out14, decoder_1_out15, decoder_1_out16,
       decoder_1_out17, decoder_1_out18, decoder_1_out19, decoder_1_out20, decoder_1_out21, decoder_1_out22,
       decoder_1_out23, decoder_1_out24, decoder_1_out25, decoder_1_out26, decoder_1_out27, IS_ALU,
       j_k_ff_1_q, j_k_ff_2_q, PC_INC, RST, ST0, ST1, ST2, ST3, undriven;
  wire [4:0] bit_extender_1_out;
  wire [5:0] OPCODE;
  wire [15:0] enable16_1_outp, enable16_2_outp, IMM16, OUTP, REG_IN;

  Decoder #(.select(5)) decoder_1 (
    .out0(PC_INC), .out8(decoder_1_out8), .out9(decoder_1_out9), .out14(decoder_1_out14),
    .out15(decoder_1_out15), .out16(decoder_1_out16), .out17(decoder_1_out17), .out18(decoder_1_out18),
    .out19(decoder_1_out19), .out20(decoder_1_out20), .out21(decoder_1_out21), .out22(decoder_1_out22),
    .out23(decoder_1_out23), .out24(decoder_1_out24), .out25(decoder_1_out25), .out26(decoder_1_out26),
    .out27(decoder_1_out27), .sel(bit_extender_1_out), .en(1'b1));  // open: out1, out2, out3, out4, out5, out6, out7, out10, out11, out12, out13, out28, out29, out30, out31
  Bit_Extender #(.in_width(6), .out_width(5)) bit_extender_1 (.in(OPCODE), .out(bit_extender_1_out));
  // Buffer ADD has open pins: in=decoder_1_out8, out=open
  // Buffer SUB has open pins: in=decoder_1_out9, out=open
  // Buffer SHR has open pins: in=decoder_1_out14, out=open
  // Buffer SHL has open pins: in=decoder_1_out15, out=open
  // Buffer ROTR has open pins: in=decoder_1_out16, out=open
  // Buffer ROTL has open pins: in=decoder_1_out17, out=open
  // Buffer SUBI has open pins: in=decoder_1_out19, out=open
  // Buffer LOAD has open pins: in=decoder_1_out20, out=open
  // Buffer STORE has open pins: in=decoder_1_out21, out=open
  // Buffer INP has open pins: in=decoder_1_out22, out=open
  // Buffer OUTP has open pins: in=decoder_1_out23, out=open
  // Buffer JUMP has open pins: in=decoder_1_out24, out=open
  // Buffer JZ has open pins: in=decoder_1_out25, out=open
  // Buffer JN has open pins: in=decoder_1_out26, out=open
  // Buffer JC has open pins: in=decoder_1_out27, out=open
  Subtractor #(.width(2)) subtractor_1 (.b(2'b10));  // open: a, out, bin, bout
  and and_1 (ST1, j_k_ff_1_q, j_k_ff_2_q);
  J_K_Flip_Flop j_k_ff_1 (.J(1'b1), .K(1'b1), .clk(CLK), .Q(j_k_ff_1_q), .reset(RST));  // open: Qn, preset
  and and_2 (ST2, ~j_k_ff_1_q, j_k_ff_2_q);  // AND_Gate
  enable16 enable16_1 (.ENA(undriven), .I(IMM16), .OUTP(enable16_1_outp));
  enable16 enable16_2 (.ENA(IS_ALU), .I(OUTP), .OUTP(enable16_2_outp));
  J_K_Flip_Flop j_k_ff_2 (.J(1'b1), .K(1'b1), .clk(j_k_ff_1_q), .Q(j_k_ff_2_q), .reset(RST));  // open: Qn, preset
  and and_3 (ST3, j_k_ff_1_q, ~j_k_ff_2_q);  // AND_Gate
  and and_4 (ST0, ~ST1, ~ST2, ~ST3);  // AND_Gate
  assign REG_IN = enable16_1_outp | enable16_2_outp;  // OR_Gate or_1, 16 bits wide

  // Other names for the same wires on the sheet: PC_SET = PC_INC

  // Notes on the sheet:
  //   ADDI
  //   NOP
endmodule
